// Logisim project 24116067_Project2 2 (2).circ as structural Verilog: 11 circuits, main circuit main
module main (
  input  reset
);

  wire branch_comp_1_beq, branch_comp_1_blt, branch_comp_1_bltu, clk, control_1_branch_tk, control_1_imm_tk,
       control_1_mem_we, control_1_pc_tk, control_1_reg_we, funct7;
  wire [1:0] control_1_reg_sel;
  wire [2:0] funct3;
  wire [3:0] alu_controller_1_alusel;
  wire [4:0] instruction_memory_1_instruction, instruction_memory_1_instruction_2,
       instruction_memory_1_instruction_3;
  wire [6:0] op_code;
  wire [31:0] alu_1_aluout, data_memory_1_rd_data, immgen_1_imm, multiplexer_1_out, multiplexer_2_out,
       multiplexer_3_out, multiplexer_4_out, next_pc_calc_1_next_pc, pc_1_pc_next, regfile_1_rs1_imfo,
       regfile_1_rs2_imfo;
  wire [31:25] instruction_memory_1_instruction_4;

  Multiplexer #(.width(32)) multiplexer_1 (
    .in0(next_pc_calc_1_next_pc), .in1(alu_1_aluout), .out(multiplexer_1_out), .sel(control_1_branch_tk));
  Clock clock_1 (.out(clk));
  pc pc_1 (.pc_in(multiplexer_1_out), .clock_pulse(clk), .reset(reset), .pc_next(pc_1_pc_next));
  // Probe on pc_1_pc_next
  Next_pc_Calc next_pc_calc_1 (.pc(pc_1_pc_next), .next_pc(next_pc_calc_1_next_pc));
  Instruction_memory instruction_memory_1 (
    .addr(pc_1_pc_next),
    .instruction({instruction_memory_1_instruction_4[31], funct7, instruction_memory_1_instruction_4[29:25], instruction_memory_1_instruction_3, instruction_memory_1_instruction_2, funct3, instruction_memory_1_instruction, op_code}));
  control control_1 (
    .op_code(op_code), .funct3(funct3), .bltu(branch_comp_1_bltu), .blt(branch_comp_1_blt),
    .beq(branch_comp_1_beq), .reg_sel(control_1_reg_sel), .imm_tk(control_1_imm_tk),
    .mem_we(control_1_mem_we), .reg_we(control_1_reg_we), .pc_tk(control_1_pc_tk),
    .branch_tk(control_1_branch_tk));
  immGen immgen_1 (
    .instr({instruction_memory_1_instruction_4[31], funct7, instruction_memory_1_instruction_4[29:25], instruction_memory_1_instruction_3, instruction_memory_1_instruction_2, funct3, instruction_memory_1_instruction, op_code}),
    .imm(immgen_1_imm));
  RegFile regfile_1 (
    .rd(instruction_memory_1_instruction), .rs1(instruction_memory_1_instruction_2),
    .rs2(instruction_memory_1_instruction_3), .wr_data(multiplexer_4_out), .wr_en(control_1_reg_we),
    .clk(clk), .reset(reset), .rs1_imfo(regfile_1_rs1_imfo), .rs2_imfo(regfile_1_rs2_imfo));
  branch_comp branch_comp_1 (
    .A(regfile_1_rs1_imfo), .B(regfile_1_rs2_imfo), .beq(branch_comp_1_beq), .blt(branch_comp_1_blt),
    .bltu(branch_comp_1_bltu));
  alu_controller alu_controller_1 (
    .funct3(funct3), .funct7(funct7), .op_code(op_code), .ALUSel(alu_controller_1_alusel));
  Multiplexer #(.width(32)) multiplexer_2 (
    .in0(regfile_1_rs2_imfo), .in1(immgen_1_imm), .out(multiplexer_2_out), .sel(control_1_imm_tk));
  Multiplexer #(.width(32)) multiplexer_3 (
    .in0(regfile_1_rs1_imfo), .in1(pc_1_pc_next), .out(multiplexer_3_out), .sel(control_1_pc_tk));
  alu alu_1 (.A(multiplexer_3_out), .B(multiplexer_2_out), .ALUSel(alu_controller_1_alusel), .ALUOut(alu_1_aluout));
  data_memory data_memory_1 (
    .w_enable(control_1_mem_we), .clk(clk), .write_data(regfile_1_rs2_imfo), .funct3(funct3),
    .addr(alu_1_aluout), .rd_data(data_memory_1_rd_data));
  Multiplexer #(.select(2), .width(32)) multiplexer_4 (
    .in0(data_memory_1_rd_data), .in1(alu_1_aluout), .in2(next_pc_calc_1_next_pc), .in3(immgen_1_imm),
    .out(multiplexer_4_out), .sel(control_1_reg_sel));
endmodule

module pc (
  input  [31:0] pc_in,
  input  clock_pulse,
  input  reset,
  output [31:0] pc_next
);

  Register #(.width(32)) register_1 (.D(pc_in), .en(1'b1), .clk(clock_pulse), .Q(pc_next), .clr(reset));
endmodule

module Instruction_memory (
  input  [31:0] addr,
  output [31:0] instruction
);

  ROM #(.addrWidth(24), .dataWidth(32)) rom_1 (.addr(addr[25:2]), .data(instruction));

  // Notes on the sheet:
  //   contents of rom_1 (hex, n*v repeats v):
  //   123450b7 10117 f00193 a00213 404182b3 41f333 41e3b3 4000413 742023 428463 429463 3e700493 c0056f
  //   37800593 6f 50067
endmodule

module Next_pc_Calc (
  input  [31:0] pc,
  output [31:0] next_pc
);

  Adder #(.width(32)) adder_1 (.a(pc), .b(32'h4), .out(next_pc));  // open: cin, cout
endmodule

module control (
  input  [6:0] op_code,
  input  [2:0] funct3,
  input  bltu,
  input  blt,
  input  beq,
  output [1:0] reg_sel,
  output imm_tk,
  output mem_we,
  output reg_we,
  output pc_tk,
  output branch_tk
);

  wire and_1_out, multiplexer_1_out, not_1_out, not_2_out, not_3_out, pla_2_out;
  wire [6:6] pla_1_out;

  PLA #(.in_width(7), .out_width(7), .\table ("0010011 0101001\n0110011 0100001\n0110111 0100011\n1100111 1101010\n1101111 1101110\n0010111 0101101\n0000011 0101000\n0100011 0011000\n1100011 1001100")) pla_1 (
    .in(op_code), .out({pla_1_out[6], reg_we, mem_we, imm_tk, pc_tk, reg_sel}));
  not not_1 (not_1_out, bltu);
  not not_2 (not_2_out, blt);
  not not_3 (not_3_out, beq);
  Multiplexer #(.select(3)) multiplexer_1 (
    .in0(beq), .in1(not_3_out), .in4(blt), .in5(not_2_out), .in6(bltu), .in7(not_1_out),
    .out(multiplexer_1_out), .sel(funct3));  // open: in2, in3
  PLA #(.in_width(7), .out_width(1), .\table ("1101111 1\n1100111 1")) pla_2 (.in(op_code), .out(pla_2_out));
  and and_1 (and_1_out, pla_1_out[6], multiplexer_1_out);
  or or_1 (branch_tk, pla_2_out, and_1_out);
endmodule

module alu (
  input  [31:0] A,
  input  [31:0] B,
  input  [3:0] ALUSel,
  output [31:0] ALUOut
);

  wire comparator_1_lt, comparator_2_lt;
  wire [31:0] adder_1_out, and_1_out, bit_extender_1_out, bit_extender_2_out, or_1_out, shifter_1_out,
       shifter_2_out, shifter_3_out, subtractor_1_out, xor_1_out;

  Adder #(.width(32)) adder_1 (.a(A), .b(B), .out(adder_1_out));  // open: cin, cout
  Subtractor #(.width(32)) subtractor_1 (.a(A), .b(B), .out(subtractor_1_out));  // open: bin, bout
  assign and_1_out = A & B;  // AND_Gate and_1, 32 bits wide
  assign or_1_out = A | B;  // OR_Gate or_1, 32 bits wide
  assign xor_1_out = A ^ B;  // XOR_Gate xor_1, 32 bits wide
  Shifter #(.width(32)) shifter_1 (.in(A), .\dist (B[4:0]), .out(shifter_1_out));
  Shifter #(.shift("lr"), .width(32)) shifter_2 (.in(A), .\dist (B[4:0]), .out(shifter_2_out));
  Shifter #(.shift("ar"), .width(32)) shifter_3 (.in(A), .\dist (B[4:0]), .out(shifter_3_out));
  Comparator #(.width(32)) comparator_1 (.a(A), .b(B), .lt(comparator_1_lt));  // open: gt, eq
  Comparator #(.mode("unsigned"), .width(32)) comparator_2 (.a(A), .b(B), .lt(comparator_2_lt));  // open: gt, eq
  assign bit_extender_1_out = {{31{1'b0}}, comparator_1_lt};  // Bit_Extender bit_extender_1
  assign bit_extender_2_out = {{31{1'b0}}, comparator_2_lt};  // Bit_Extender bit_extender_2
  Multiplexer #(.select(4), .width(32)) multiplexer_1 (
    .in0(adder_1_out), .in1(shifter_1_out), .in2(bit_extender_1_out), .in3(bit_extender_2_out),
    .in4(xor_1_out), .in5(shifter_2_out), .in6(or_1_out), .in7(and_1_out), .in8(subtractor_1_out),
    .in13(shifter_3_out), .out(ALUOut), .sel(ALUSel));  // open: in9, in10, in11, in12, in14, in15
endmodule

module alu_controller (
  input  [2:0] funct3,
  input  funct7,
  input  [6:0] op_code,
  output [3:0] ALUSel
);

  PLA #(.in_width(11), .out_width(4), .\table ("0000011xxxx 0000\n0100011xxxx 0000\n1100011xxxx 0000\n0010011000x 0000\n0010011001x 0001\n0010011010x 0010\n0010011011x 0011\n0010011100x 0100\n00100111010 0101\n00100111011 1101\n0010011110x 0110\n0010011111x 0111\n01100110000 0000\n01100110001 1000\n0110011001x 0001\n0110011010x 0010\n0110011011x 0011\n0110011100x 0100\n01100111010 0101\n01100111011 1101\n0110011110x 0110\n0110011111x 0111")) pla_1 (
    .in({op_code, funct3, funct7}), .out(ALUSel));
endmodule

module branch_comp (
  input  [31:0] A,
  input  [31:0] B,
  output beq,
  output blt,
  output bltu
);

  Comparator #(.width(32)) comparator_1 (.a(A), .b(B), .eq(beq), .lt(blt));  // open: gt
  Comparator #(.mode("unsigned"), .width(32)) comparator_2 (.a(A), .b(B), .lt(bltu));  // open: gt, eq
endmodule

module RegFile (
  input  [4:0] rd,
  input  [4:0] rs1,
  input  [4:0] rs2,
  input  [31:0] wr_data,
  input  wr_en,
  input  clk,
  input  reset,
  output [31:0] rs1_imfo,
  output [31:0] rs2_imfo
);

  wire x0we, x1we, x2we, x3we, x4we, x5we, x6we, x7we, x8we, x9we, x10we, x11we, x12we, x13we, x14we, x15we,
       x16we, x17we, x18we, x19we, x20we, x21we, x22we, x23we, x24we, x25we, x26we, x27we, x28we, x29we,
       x30we, x31we;
  wire [31:0] x0q, x1q, x2q, x3q, x4q, x5q, x6q, x7q, x8q, x9q, x10q, x11q, x12q, x13q, x14q, x15q, x16q,
       x17q, x18q, x19q, x20q, x21q, x22q, x23q, x24q, x25q, x26q, x27q, x28q, x29q, x30q, x31q;

  Demultiplexer #(.select(5)) demultiplexer_1 (
    .out0(x0we), .out1(x1we), .out2(x2we), .out3(x3we), .out4(x4we), .out5(x5we), .out6(x6we), .out7(x7we),
    .out8(x8we), .out9(x9we), .out10(x10we), .out11(x11we), .out12(x12we), .out13(x13we), .out14(x14we),
    .out15(x15we), .out16(x16we), .out17(x17we), .out18(x18we), .out19(x19we), .out20(x20we), .out21(x21we),
    .out22(x22we), .out23(x23we), .out24(x24we), .out25(x25we), .out26(x26we), .out27(x27we), .out28(x28we),
    .out29(x29we), .out30(x30we), .out31(x31we), .in(wr_en), .sel(rd));
  Register #(.width(32)) x0 (.D(wr_data), .en(1'b0), .clk(clk), .Q(x0q), .clr(reset));
  Register #(.width(32)) x4 (.D(wr_data), .en(x4we), .clk(clk), .Q(x4q), .clr(reset));
  Register #(.width(32)) x8 (.D(wr_data), .en(x8we), .clk(clk), .Q(x8q), .clr(reset));
  Register #(.width(32)) x12 (.D(wr_data), .en(x12we), .clk(clk), .Q(x12q), .clr(reset));
  Register #(.width(32)) x16 (.D(wr_data), .en(x16we), .clk(clk), .Q(x16q), .clr(reset));
  Register #(.width(32)) x20 (.D(wr_data), .en(x20we), .clk(clk), .Q(x20q), .clr(reset));
  Register #(.width(32)) x24 (.D(wr_data), .en(x24we), .clk(clk), .Q(x24q), .clr(reset));
  Register #(.width(32)) x28 (.D(wr_data), .en(x28we), .clk(clk), .Q(x28q), .clr(reset));
  Register #(.width(32)) x1 (.D(wr_data), .en(x1we), .clk(clk), .Q(x1q), .clr(reset));
  Register #(.width(32)) x5 (.D(wr_data), .en(x5we), .clk(clk), .Q(x5q), .clr(reset));
  Register #(.width(32)) x9 (.D(wr_data), .en(x9we), .clk(clk), .Q(x9q), .clr(reset));
  Register #(.width(32)) x13 (.D(wr_data), .en(x13we), .clk(clk), .Q(x13q), .clr(reset));
  Register #(.width(32)) x17 (.D(wr_data), .en(x17we), .clk(clk), .Q(x17q), .clr(reset));
  Register #(.width(32)) x21 (.D(wr_data), .en(x21we), .clk(clk), .Q(x21q), .clr(reset));
  Register #(.width(32)) x25 (.D(wr_data), .en(x25we), .clk(clk), .Q(x25q), .clr(reset));
  Register #(.width(32)) x29 (.D(wr_data), .en(x29we), .clk(clk), .Q(x29q), .clr(reset));
  Register #(.width(32)) x2 (.D(wr_data), .en(x2we), .clk(clk), .Q(x2q), .clr(reset));
  Register #(.width(32)) x6 (.D(wr_data), .en(x6we), .clk(clk), .Q(x6q), .clr(reset));
  Register #(.width(32)) x10 (.D(wr_data), .en(x10we), .clk(clk), .Q(x10q), .clr(reset));
  Register #(.width(32)) x14 (.D(wr_data), .en(x14we), .clk(clk), .Q(x14q), .clr(reset));
  Register #(.width(32)) x18 (.D(wr_data), .en(x18we), .clk(clk), .Q(x18q), .clr(reset));
  Register #(.width(32)) x22 (.D(wr_data), .en(x22we), .clk(clk), .Q(x22q), .clr(reset));
  Register #(.width(32)) x26 (.D(wr_data), .en(x26we), .clk(clk), .Q(x26q), .clr(reset));
  Register #(.width(32)) x30 (.D(wr_data), .en(x30we), .clk(clk), .Q(x30q), .clr(reset));
  Register #(.width(32)) x3 (.D(wr_data), .en(x3we), .clk(clk), .Q(x3q), .clr(reset));
  Register #(.width(32)) x7 (.D(wr_data), .en(x7we), .clk(clk), .Q(x7q), .clr(reset));
  Register #(.width(32)) x11 (.D(wr_data), .en(x11we), .clk(clk), .Q(x11q), .clr(reset));
  Register #(.width(32)) x15 (.D(wr_data), .en(x15we), .clk(clk), .Q(x15q), .clr(reset));
  Register #(.width(32)) x19 (.D(wr_data), .en(x19we), .clk(clk), .Q(x19q), .clr(reset));
  Register #(.width(32)) x23 (.D(wr_data), .en(x23we), .clk(clk), .Q(x23q), .clr(reset));
  Register #(.width(32)) x27 (.D(wr_data), .en(x27we), .clk(clk), .Q(x27q), .clr(reset));
  Register #(.width(32)) x31 (.D(wr_data), .en(x31we), .clk(clk), .Q(x31q), .clr(reset));
  Multiplexer #(.select(5), .width(32)) multiplexer_1 (
    .in0(x0q), .in1(x1q), .in2(x2q), .in3(x3q), .in4(x4q), .in5(x5q), .in6(x6q), .in7(x7q), .in8(x8q),
    .in9(x9q), .in10(x10q), .in11(x11q), .in12(x12q), .in13(x13q), .in14(x14q), .in15(x15q), .in16(x16q),
    .in17(x17q), .in18(x18q), .in19(x19q), .in20(x20q), .in21(x21q), .in22(x22q), .in23(x23q), .in24(x24q),
    .in25(x25q), .in26(x26q), .in27(x27q), .in28(x28q), .in29(x29q), .in30(x30q), .in31(x31q),
    .out(rs1_imfo), .sel(rs1));
  Multiplexer #(.select(5), .width(32)) multiplexer_2 (
    .in0(x0q), .in1(x1q), .in2(x2q), .in3(x3q), .in4(x4q), .in5(x5q), .in6(x6q), .in7(x7q), .in8(x8q),
    .in9(x9q), .in10(x10q), .in11(x11q), .in12(x12q), .in13(x13q), .in14(x14q), .in15(x15q), .in16(x16q),
    .in17(x17q), .in18(x18q), .in19(x19q), .in20(x20q), .in21(x21q), .in22(x22q), .in23(x23q), .in24(x24q),
    .in25(x25q), .in26(x26q), .in27(x27q), .in28(x28q), .in29(x29q), .in30(x30q), .in31(x31q),
    .out(rs2_imfo), .sel(rs2));

  // Other names for the same wires on the sheet: clk_t = clk; rd_t[31:0] = wr_data; rse = reset
endmodule

module immGen (
  input  [31:0] instr,
  output [31:0] imm
);

  wire [2:0] pla_1_out;
  wire [31:0] bit_extender_1_out, bit_extender_2_out, bit_extender_3_out, bit_extender_4_out;

  PLA #(.in_width(7), .out_width(3), .\table ("0000011 000\n0010011 000\n1100111 000\n0100011 001\n1100011 010\n0110111 011\n0010111 011\n1101111 100")) pla_1 (
    .in(instr[6:0]), .out(pla_1_out));
  assign bit_extender_1_out = {{20{instr[31]}}, instr[31:20]};  // Bit_Extender bit_extender_1
  assign bit_extender_2_out = {{20{instr[31]}}, {instr[31:25], instr[11:7]}};  // Bit_Extender bit_extender_2
  assign bit_extender_3_out = {{19{instr[31]}}, {instr[31], instr[7], instr[30:25], instr[11:8], 1'b0}};  // Bit_Extender bit_extender_3
  assign bit_extender_4_out = {{11{instr[31]}}, {instr[31], instr[19:12], instr[20], instr[30:21], 1'b0}};  // Bit_Extender bit_extender_4
  Multiplexer #(.select(3), .width(32)) multiplexer_1 (
    .in0(bit_extender_1_out), .in1(bit_extender_2_out), .in2(bit_extender_3_out),
    .in3({instr[31:12], {12{1'b0}}}), .in4(bit_extender_4_out), .out(imm), .sel(pla_1_out));  // open: in5, in6, in7
endmodule

module data_memory (
  input  w_enable,
  input  clk,
  input  [31:0] write_data,
  input  [2:0] funct3,
  input  [31:0] addr,
  output [31:0] rd_data
);

  wire [3:0] pla_1_out;
  wire [31:0] bit_extender_1_out, bit_extender_2_out, bit_extender_3_out, bit_extender_4_out, ram_1_dout,
       shifter_1_out, shifter_2_out;

  PLA #(.in_width(6), .out_width(4), .\table ("100100 0011\n100110 1100\n100000 0001\n100001 0010\n100010 0100\n100011 1000\n1010xx 1111")) pla_1 (
    .in({w_enable, funct3, addr[1:0]}), .out(pla_1_out));
  Shifter #(.width(32)) shifter_1 (.in(write_data), .\dist ({addr[1:0], 3'b000}), .out(shifter_1_out));
  RAM #(.addrWidth(20), .asyncread("true"), .byteenables("byteEnables"), .dataWidth(32)) ram_1 (
    .addr(addr[21:2]), .we(w_enable), .oe(1'b1), .clk(clk), .din(shifter_1_out), .dout(ram_1_dout),
    .be3(pla_1_out[3]), .be2(pla_1_out[2]), .be1(pla_1_out[1]), .be0(pla_1_out[0]));
  Shifter #(.shift("lr"), .width(32)) shifter_2 (.in(ram_1_dout), .\dist ({addr[1:0], 3'b000}), .out(shifter_2_out));
  assign bit_extender_1_out = {{16{shifter_2_out[15]}}, shifter_2_out[15:0]};  // Bit_Extender bit_extender_1
  assign bit_extender_2_out = {{16{1'b0}}, shifter_2_out[15:0]};  // Bit_Extender bit_extender_2
  assign bit_extender_3_out = {{24{shifter_2_out[7]}}, shifter_2_out[7:0]};  // Bit_Extender bit_extender_3
  assign bit_extender_4_out = {{24{1'b0}}, shifter_2_out[7:0]};  // Bit_Extender bit_extender_4
  Multiplexer #(.select(3), .width(32)) multiplexer_1 (
    .in0(bit_extender_3_out), .in1(bit_extender_1_out), .in2(shifter_2_out), .in4(bit_extender_4_out),
    .in5(bit_extender_2_out), .out(rd_data), .sel(funct3));  // open: in3, in6, in7
endmodule
